# Fritzing sketch reed-sensor (saved by Fritzing 0.9.2b)
breadboards: 1

parts:
  S2 = SWITCH-MOMENTARY-2 [package=reed_switch_plastic]
  Raspberry_Pi1 = Raspberry Pi 2

nets:
  N1: S2.1, Raspberry_Pi1.GPIO24
  N2: S2.2, Raspberry_Pi1.GND
